# Fritzing sketch untz (saved by Fritzing 0.9.3b)

parts:
  Part3 = Trellis Monochrome Driver PCB for 4x4 Keypad and 3mm LEDs [part_number=1616]
  Part4 = Trellis Monochrome Driver PCB for 4x4 Keypad and 3mm LEDs [part_number=1616]  # not connected
  Part5 = Trellis Monochrome Driver PCB for 4x4 Keypad and 3mm LEDs [part_number=1616]  # not connected
  Part6 = Trellis Monochrome Driver PCB for 4x4 Keypad and 3mm LEDs [part_number=1616]  # not connected
  Part2 = Arduino Musical Instrument Shield
  SPKR1 = Loudspeaker
  Part7 = Adafruit Stereo 2.8W Class D Audio Amplifier - I2C Control AGC - TPA2016 [part_number="Adafruit #1712"]
  ENCODER1 = Rotary Encoder with Knob
  ENCODER2 = Rotary Encoder with Knob
  ENCODER3 = Rotary Encoder with Knob
  ENCODER4 = Rotary Encoder with Knob
  Part8 = Arduino Leonardo (Rev3b)

nets:
  VCC: Part3.VCC, Part8.5V
  GND: Part3.GND, ENCODER1.no_name_yet#5, ENCODER2.no_name_yet#5, ENCODER3.no_name_yet#5, ENCODER4.no_name_yet#5, Part8.GND
  N1: Part3.SCL, Part8.SCL
  N2: Part3.SDA, Part8.SDA
  N3: Part2.GBUF, Part7.IN_L_N, Part7.SCL
  N4: Part2.LEFT, Part7.IN_L_P
  N5: Part2.MIDI-IN, Part8.D4/A6
  GND_2: Part2.GND, Part7.GND, Part7.SHUTDOWN
  VIN: Part2.VIN, Part8.VIN
  N6: SPKR1.pin1, Part7.OUT_L_N
  N7: SPKR1.pin2, Part7.OUT_L_P
  VDD: Part7.VDD, Part8.3V3
  N8: ENCODER1.no_name_yet#1, Part8.D5_PWM
  N9: ENCODER1.no_name_yet#2, ENCODER2.no_name_yet#2, ENCODER3.no_name_yet#2, ENCODER4.no_name_yet#2
  N10: ENCODER1.no_name_yet#3, Part8.A4
  N11: ENCODER1.no_name_yet#4, Part8.D0/RX
  N12: ENCODER2.no_name_yet#1, Part8.D7
  N13: ENCODER2.no_name_yet#3, Part8.D6_PWM/A7
  N14: ENCODER2.no_name_yet#4, Part8.D12/A11
  N15: ENCODER3.no_name_yet#1, Part8.D9_PWM/A9
  N16: ENCODER3.no_name_yet#3, Part8.D8/A8
  N17: ENCODER3.no_name_yet#4, Part8.D1/TX
  N18: ENCODER4.no_name_yet#1, Part8.D11_PWM
  N19: ENCODER4.no_name_yet#3, Part8.D10_PWM/A10
  N20: ENCODER4.no_name_yet#4, Part8.A5

notes:
  This shows the Trellis array from the front but the pinout order is from the back

custom parts:
  Trellis Monochrome Driver PCB for 4x4 Keypad and 3mm LEDs: Trellis is an open source backlight keypad driver system. It is easy to use, works with any 3mm LEDs and eight tiles can be tiled together on a shared I2C bus. This PCB is specially made to match the Adafruit 4x4 elastomer keypad. Each Trellis PCB has 4x4 pads and 4x4 matching spots for 3mm LEDs. The circuitry on-board handles the background key-presses and LED lighting for the 4x4 tile.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
  Adafruit Stereo 2.8W Class D Audio Amplifier - I2C Control AGC - TPA2016: A mini class D with AGC and I2C control? Yes please! This incredibly small stereo amplifier is surprisingly powerful. It is able to deliver 2 x 2.8W channels into 4 ohm impedance speakers (@ 10% THD) and it has a i2c control interface as well as an AGC (automatic gain control) system to keep your audio from clipping or distorting. If you don't want to use I2C to control it, it does start up on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
  Rotary Encoder with Knob: Rotary Encoder with 1/4" Shaft and Knob
